# Fritzing sketch fritzing shema (saved by Fritzing 0.9.3b)
breadboards: 2

parts:
  esp1 = ESP32 DevKitc V4
  Part1 = HC-SR501 Body Sensor Module
  Part2 = Arduino Uno (Rev3)
  LED1 = LED - 5mm [color="Red (633nm)" package="5 mm [THT]"]
  J1 = Piezo Speaker
  S3 = Momentary Switch [package=ksa_sealed_tac_switch]
  R2 = Resistor [tolerance=±5% resistance=220 package="2512 [SMD]"]
  R3 = Resistor [tolerance=±5% resistance=1k package="2512 [SMD]"]
  part = Water Level Sensor
  Mod1 = KY-015 Temperature & Humidity Sensor Module [package="Breakout board"]
  R4 = Resistor [tolerance=±5% resistance=2.2k package=THT]
  R5 = Resistor [tolerance=±5% resistance=1k package=THT]
  J2 = Basic Servo
  Part3 = RFID-RC522-v2

nets:
  N1: esp1.IO16, R4.Pin_1, R5.Pin_0
  N2: esp1.IO17, Part2.D0/RX
  N3: esp1.IO5, Part3.SDA
  N4: esp1.IO18, Part3.SCK
  N5: esp1.IO19, Part3.MISO
  N6: esp1.IO23, Part3.MOSI
  GND: esp1.GND, Part1.GND, Part2.GND, LED1.cathode, J1.pin1, R3.Pin_0, part.GND, Mod1.-, R4.Pin_0, J2.gnd, Part3.GND
  3V3: esp1.3V3, Part3.3.3V
  N7: esp1.IO32, J2.pulse
  N8: esp1.IO27, Part3.RST
  5V: esp1.5V, J2.vcc
  VCC: Part1.VCC, Part2.5V, S3.2, part.VCC, Mod1.Vin
  N9: Part1.OUT, Part2.D7
  N10: Part2.A0, part.SIG
  N11: Part2.D12/MISO, S3.3
  N12: Part2.D1/TX, R5.Pin_1
  N13: Part2.D2, Mod1.S
  N14: Part2.D5_PWM, J1.pin2
  N15: Part2.D6_PWM, R2.Pin_1
  N16: LED1.anode, R2.Pin_0
  N17: S3.4, R3.Pin_1

custom parts:
  ESP32 DevKitc V4: ESP32-DevKitC board with ESP32-WROOM-32 module. ESP32-DevKitC V4 is a small-sized ESP32-based development board produced by Espressif. Most of the pins on the ESP module are broken out to the pin headers on the board. The pins D0, D1, D2, D3, CMD and CLK are used internally for communication between ESP32 and SPI flash memory. They are grouped on both sides near the USB connector. Avoid using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
  HC-SR501 Body Sensor Module: Pyroelectric Infrared PIR Motion Sensor Detector Module
  Water Level Sensor: A water level sensor. This sensor operates at 3V to 5V. The Sig (signal) pin outputs an analogue signal that is in proportion to the amount of water in contact with the sensor.
  KY-015 Temperature & Humidity Sensor Module: KY-015 temperature and humidity sensor module, provides a low-latency serial interface to measure humidity and temperature.
  RFID-RC522-v2: A simple China made RFID-RC522 Reader; do check the pin labels, as this is a MFRC522 based clone.

// code stored in the sketch: Untitled3.ino

